# Fritzing sketch BigBreadBoard (saved by Fritzing 0.9.4)
breadboards: 3

parts:
  Breadboard4 = Breadboard Split Power
  Breadboard5 = Breadboard Split Power
  Teensy_3_1 = Teensy 3.1  # not connected
  RG_encoder1 = SprkFn RG Encoder [package="DIP (Dual Inline) [THT]"]
  WS2812B1 = WS2812B NP [package="DIP (Dual Inline) [THT]"]
  WS2812B2 = WS2812B NP [package="DIP (Dual Inline) [THT]"]
  WS2812B3 = WS2812B NP [package="DIP (Dual Inline) [THT]"]
  WS2812B4 = WS2812B NP [package="DIP (Dual Inline) [THT]"]
  OLED_I2C1 = OLED 128x64 I2C Monochrome Display
  M1 = BMP280
  WIZ820io1 = WIZ820io [part_number=WIZ820io]
  OLED_I2C2 = OLED 128x64 I2C Monochrome Display
  Part1 = 12 NeoPixel Ring [part_number=1643]
  S2 = Pushbutton [package="[THT]"]
  S3 = Pushbutton [package="[THT]"]
  S4 = Pushbutton [package="[THT]"]
  R1 = Resistor [tolerance=±5% resistance=220 package="2512 [SMD]"]
  R2 = Resistor [tolerance=±5% resistance=220 package="2512 [SMD]"]
  R3 = Resistor [tolerance=±5% resistance=220 package="2512 [SMD]"]

nets:
  5V: Breadboard4.pin3Y, Breadboard4.pin15Y, Breadboard4.pin17Y, Breadboard4.pin21Y, Breadboard4.pin29Y, Breadboard5.pin3Y, Breadboard5.pin12Y, Breadboard5.pin14Y, Breadboard5.pin15Y, Breadboard5.pin17Y, Breadboard5.pin29Y, WS2812B1.5V, WS2812B2.5V, WS2812B3.5V, WS2812B4.5V, OLED_I2C1.VDD, M1.VIN, WIZ820io1.VIN, OLED_I2C2.VDD, Part1.VDD, S2.Pin_1, S2.Pin_2, S3.Pin_1, S3.Pin_2, S4.Pin_3, S4.Pin_4
  GND: Breadboard4.pin3Z, Breadboard4.pin20Z, Breadboard4.pin29Z, Breadboard5.pin3Z, Breadboard5.pin11Z, Breadboard5.pin27Z, Breadboard5.pin28Z, RG_encoder1.B, WS2812B1.GND, WS2812B2.GND, WS2812B3.GND, WS2812B4.GND, OLED_I2C1.GND, M1.GND, WIZ820io1.GND, OLED_I2C2.GND, Part1.GND, R1.Pin_1, R2.Pin_1, R3.Pin_1
  N1: WS2812B1.DO, WS2812B2.DI
  N2: WS2812B2.DO, WS2812B3.DI
  N3: WS2812B3.DO, WS2812B4.DI
  N4: WS2812B4.DO, Part1.IN
  N5: OLED_I2C1.SDA, M1.SDA, OLED_I2C2.SDA
  N6: OLED_I2C1.SCK, M1.SCL, OLED_I2C2.SCK
  N7: S2.Pin_3, S2.Pin_4
  N8: S3.Pin_3, S3.Pin_4, R2.Pin_0
  N9: S4.Pin_1, S4.Pin_2, R3.Pin_0

custom parts:
  Breadboard Split Power: A custom 6 pin per group power supply strip where the top row (ground) is all bussed together and the bottom row (+V) is split in two groups of 12 pins. This version is modified to be a loadable part and was rescaled to be on the standard 1px = 1thou grid with the size set in inches
  SprkFn RG Encoder: SparkFun RG Rotary Encoder
  WS2812B NP: WS2812B Adafruit Breakout Neopixel
  BMP280: Temperature Humidity Barometric presure Sensor, I2C
  12 NeoPixel Ring: 12 ultra bright smart LED NeoPixels are arranged in a circle with 1.5" (37mm) outer diameter. The rings are 'chainable' - connect the output pin of one to the input pin of another. Use only one microcontroller pin to control as many as you can chain together! Each LED is addressable as the driver chip is inside the LED. Each one has ~18mA constant current drive so the color will be very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
  Pushbutton: A generic pushbutton.
  Pushbutton: A generic pushbutton.
  Pushbutton: A generic pushbutton.
